// Logisim project TallerLogica-Combinatorios.circ as structural Verilog: 13 circuits, main circuit verificador
module sumador_simple (
  input  A,
  input  B,
  input  carryIn,
  input  [3:0] a_2,
  input  [3:0] b_2,
  output S,
  output out_7,
  output Cout,
  output final_Sum,
  output out_10
);

  wire and_2_out, and_3_out, and_4_out, and_6_out, undriven, undriven_2, undriven_3, undriven_4, undriven_5,
       undriven_6, undriven_7;

  xor xor_1 (S, A, B);
  and and_1 (Cout, B, A);
  and and_2 (and_2_out, undriven_3, undriven_4);
  and and_3 (and_3_out, undriven_5, undriven_6);
  and and_4 (and_4_out, undriven_2, undriven);
  and and_5 (out_7, and_2_out, and_3_out);
  xor xor_2 (final_Sum, undriven_7, carryIn);
  and and_6 (and_6_out, carryIn, undriven_7);
  or or_1 (out_10, and_6_out, and_4_out);

  // Notes on the sheet:
  //   Comparador con 0000
  //   sum'
  //   carry'
  //   final Carry
endmodule

module sumador_completo (
  input  A,
  input  B,
  input  Cin,
  output S,
  output Cout
);

  wire and_1_out, and_2_out, xor_1_out;

  xor xor_1 (xor_1_out, A, B);
  and and_1 (and_1_out, B, A);
  xor xor_2 (S, xor_1_out, Cin);
  and and_2 (and_2_out, Cin, xor_1_out);
  or or_1 (Cout, and_2_out, and_1_out);

  // Notes on the sheet:
  //   sum'
  //   carry'
  //   final Sum
  //   final Carry
endmodule

module sumador_4 (
  input  Cin,
  input  [3:0] A,
  input  [3:0] B,
  output [3:0] S,
  output Cout,
  output AnteUltimoCarry
);

  wire sumador_completo_1_cout, sumador_completo_2_cout;

  sumador_completo sumador_completo_1 (.A(A[0]), .B(B[0]), .Cin(Cin), .S(S[0]), .Cout(sumador_completo_1_cout));
  sumador_completo sumador_completo_2 (
    .A(A[1]), .B(B[1]), .Cin(sumador_completo_1_cout), .S(S[1]), .Cout(sumador_completo_2_cout));
  sumador_completo sumador_completo_3 (
    .A(A[2]), .B(B[2]), .Cin(sumador_completo_2_cout), .S(S[2]), .Cout(AnteUltimoCarry));
  Hex_Digit_Display hex_digit_display_1 (.value(S));  // open: dp
  sumador_completo sumador_completo_4 (.A(A[3]), .B(B[3]), .Cin(AnteUltimoCarry), .S(S[3]), .Cout(Cout));
endmodule

module comparador_cero (
  input  [3:0] A,
  output Z
);

  wire and_1_out, and_2_out, not_1_out, not_2_out, not_3_out, not_4_out;

  not not_1 (not_1_out, A[0]);
  not not_2 (not_2_out, A[1]);
  not not_3 (not_3_out, A[2]);
  not not_4 (not_4_out, A[3]);
  and and_1 (and_1_out, not_1_out, not_2_out);
  and and_2 (and_2_out, not_3_out, not_4_out);
  and and_3 (Z, and_1_out, and_2_out);

  // Notes on the sheet:
  //   Comparador con 0000
endmodule

module sumador_flags (
  input  Cin,
  input  [3:0] A,
  input  [3:0] B,
  output [3:0] S,
  output N,
  output Z,
  output C,
  output V
);

  wire sumador_4_1_anteultimocarry;

  Hex_Digit_Display hex_digit_display_1 (.value({N, S[2:0]}));  // open: dp
  sumador_4 sumador_4_1 (
    .Cin(Cin), .A(A), .B(B), .S({N, S[2:0]}), .Cout(C), .AnteUltimoCarry(sumador_4_1_anteultimocarry));
  comparador_cero comparador_cero_1 (.A({N, S[2:0]}), .Z(Z));
  xor xor_1 (V, C, sumador_4_1_anteultimocarry);

  assign S[3] = N;
endmodule

module incrementador_4 (
  input  [3:0] A,
  output [3:0] S
);

  sumador_4 sumador_4_1 (.Cin(1'b1), .A(A), .S(S));  // open: B, Cout, AnteUltimoCarry
  Hex_Digit_Display hex_digit_display_1 (.value(S));  // open: dp
endmodule

module inversor_4 (
  input  [3:0] A,
  input  INV,
  output [3:0] S
);

  wire not_5_out;
  wire [3:0] incrementador_4_1_s, not_1_out;

  not not_1 (not_1_out[0], A[0]);
  not not_2 (not_1_out[1], A[1]);
  not not_3 (not_1_out[2], A[2]);
  not not_4 (not_1_out[3], A[3]);
  incrementador_4 incrementador_4_1 (.A(not_1_out), .S(incrementador_4_1_s));
  Multiplexer #(.width(4)) multiplexer_1 (.in0(incrementador_4_1_s), .in1(A), .out(S), .sel(not_5_out));
  not not_5 (not_5_out, INV);
  Hex_Digit_Display hex_digit_display_1 (.value(S));  // open: dp
endmodule

module ALU (
  input  [3:0] A,
  input  [3:0] B,
  input  [1:0] OP,
  output N,
  output Z,
  output V,
  output C,
  output [3:0] S
);

  wire and_1_out, and_2_out, and_3_out, and_4_out, comparador_1000_1_out_2, comparador_1000_2_out_2,
       comparador_1000_3_out_2, comparador_cero_1_z, comparador_cero_2_z, comparador_cero_3_z,
       es_positivo_1_out_2, es_positivo_2_out_2, es_positivo_3_out_2, multiplexer_2_out, multiplexer_4_out,
       multiplexer_5_out, not_1_out, not_2_out, not_3_out, not_4_out, or_1_out, or_2_out, sumador_flags_1_c,
       sumador_flags_1_v, sumador_flags_2_c, sumador_flags_2_v;
  wire [3:0] and_bit_a_bit_1_out_3, inversor_4_1_s, or_bit_a_bit_1_out_3, sumador_flags_1_s,
       sumador_flags_2_s;

  sumador_flags sumador_flags_1 (
    .A(A), .B(B), .S(sumador_flags_1_s), .C(sumador_flags_1_c), .V(sumador_flags_1_v));  // open: Cin, N, Z
  inversor_4 inversor_4_1 (.A(B), .INV(1'b1), .S(inversor_4_1_s));
  comparador_1000 comparador_1000_1 (.in_1(A), .out_2(comparador_1000_1_out_2));
  es_positivo es_positivo_1 (.in_1(B), .out_2(es_positivo_1_out_2));
  es_positivo es_positivo_2 (.in_1(A), .out_2(es_positivo_2_out_2));
  comparador_cero comparador_cero_1 (.A(A), .Z(comparador_cero_1_z));
  comparador_1000 comparador_1000_2 (.in_1(B), .out_2(comparador_1000_2_out_2));
  not not_1 (not_1_out, es_positivo_3_out_2);
  es_positivo es_positivo_3 (.in_1(A), .out_2(es_positivo_3_out_2));
  not not_2 (not_2_out, comparador_cero_2_z);
  comparador_cero comparador_cero_2 (.A(A), .Z(comparador_cero_2_z));
  comparador_1000 comparador_1000_3 (.in_1(B), .out_2(comparador_1000_3_out_2));
  OR_BIT_A_BIT or_bit_a_bit_1 (.in_1(A), .in_2(B), .out_3(or_bit_a_bit_1_out_3));
  or or_1 (or_1_out, es_positivo_2_out_2, comparador_cero_1_z);
  and and_1 (and_1_out, not_1_out, not_2_out);
  sumador_flags sumador_flags_2 (
    .A(A), .B(inversor_4_1_s), .S(sumador_flags_2_s), .C(sumador_flags_2_c), .V(sumador_flags_2_v));  // open: Cin, N, Z
  AND_BIT_A_BIT and_bit_a_bit_1 (.in_1(A), .in_2(B), .out_3(and_bit_a_bit_1_out_3));
  comparador_cero comparador_cero_3 (.A(B), .Z(comparador_cero_3_z));
  and and_2 (and_2_out, or_1_out, comparador_1000_2_out_2);
  and and_3 (and_3_out, and_1_out, comparador_1000_3_out_2);
  and and_4 (and_4_out, comparador_1000_1_out_2, es_positivo_1_out_2);
  or or_2 (or_2_out, and_4_out, and_2_out);
  Multiplexer #(.select(2), .width(4)) multiplexer_1 (
    .in0(sumador_flags_1_s), .in1(sumador_flags_2_s), .in2(and_bit_a_bit_1_out_3),
    .in3(or_bit_a_bit_1_out_3), .out({N, S[2:0]}), .sel(OP));
  not not_3 (not_3_out, sumador_flags_2_c);
  Hex_Digit_Display hex_digit_display_1 (.value({N, S[2:0]}));  // open: dp
  Multiplexer #(.select(2)) multiplexer_2 (
    .in0(sumador_flags_1_c), .in1(not_3_out), .in2(1'b0), .in3(1'b0), .out(multiplexer_2_out), .sel(OP));
  Multiplexer multiplexer_3 (.in0(1'b0), .in1(multiplexer_2_out), .out(C), .sel(not_4_out));
  not not_4 (not_4_out, comparador_cero_3_z);
  Multiplexer multiplexer_4 (.in0(sumador_flags_2_v), .in1(1'b1), .out(multiplexer_4_out), .sel(or_2_out));
  Multiplexer multiplexer_5 (.in0(multiplexer_4_out), .in1(1'b0), .out(multiplexer_5_out), .sel(and_3_out));
  Multiplexer #(.select(2)) multiplexer_6 (
    .in0(sumador_flags_1_v), .in1(multiplexer_5_out), .in2(1'b0), .in3(1'b0), .out(V), .sel(OP));
  comparador_cero comparador_cero_4 (.A({N, S[2:0]}), .Z(Z));

  assign S[3] = N;

  // Notes on the sheet:
  //   Caso B=-8 y A < 0 => V=0
  //   Caso B=-8 y A>=0 => V=1
  //   Caso A = -8 y (B>0) => V=1
endmodule

module verificador (
  output [3:0] out_1,
  output [3:0] out_2,
  output [1:0] out_3,
  output halt,
  output N,
  output Z,
  output V,
  output C,
  output [3:0] res
);

  wire clock_1_out;

  Clock clock_1 (.out(clock_1_out));
  Counter #(.max('h3ff), .width(10)) counter_1 (
    .clk(clock_1_out), .carry(halt), .Q({out_3, out_2, out_1}));  // open: clr, load, up, count, D
  ALU alu_1 (.A(out_1), .B(out_2), .OP(out_3), .N(N), .Z(Z), .V(V), .C(C), .S(res));
endmodule

module AND_BIT_A_BIT (
  input  [3:0] in_1,
  input  [3:0] in_2,
  output [3:0] out_3
);

  and and_1 (out_3[0], in_1[0], in_2[0]);
  and and_2 (out_3[2], in_1[2], in_2[2]);
  and and_3 (out_3[1], in_1[1], in_2[1]);
  and and_4 (out_3[3], in_1[3], in_2[3]);
endmodule

module OR_BIT_A_BIT (
  input  [3:0] in_1,
  input  [3:0] in_2,
  output [3:0] out_3
);

  or or_1 (out_3[0], in_1[0], in_2[0]);
  or or_2 (out_3[2], in_1[2], in_2[2]);
  or or_3 (out_3[1], in_1[1], in_2[1]);
  or or_4 (out_3[3], in_1[3], in_2[3]);
endmodule

module comparador_1000 (
  input  [3:0] in_1,
  output out_2
);

  wire and_1_out, and_2_out, not_1_out, not_2_out, not_3_out;

  not not_1 (not_1_out, in_1[2]);
  not not_2 (not_2_out, in_1[0]);
  not not_3 (not_3_out, in_1[1]);
  and and_1 (and_1_out, not_1_out, in_1[3]);
  and and_2 (and_2_out, not_2_out, not_3_out);
  and and_3 (out_2, and_2_out, and_1_out);
endmodule

module es_positivo (
  input  [3:0] in_1,
  output out_2
);

  wire and_1_out, comparador_cero_1_z, not_1_out, not_2_out, or_1_out;

  not not_1 (not_1_out, in_1[3]);
  or or_1 (or_1_out, in_1[0], in_1[1], in_1[2]);
  and and_1 (and_1_out, or_1_out, not_1_out);
  Multiplexer multiplexer_1 (.in0(1'b0), .in1(and_1_out), .out(out_2), .sel(not_2_out));
  not not_2 (not_2_out, comparador_cero_1_z);
  comparador_cero comparador_cero_1 (.A(in_1), .Z(comparador_cero_1_z));
endmodule
